# Fritzing sketch RPiStepMotor (saved by Fritzing 0.9.2b)
breadboards: 1

parts:
  Raspberry_Pi1 = Raspberry Pi B rev2
  IC1 = L293D [package=THT]
  M1 = Stepper Motor - Bipolar

nets:
  N1: Raspberry_Pi1.5V, IC1.Enable_1, IC1.+Vmotor, IC1.Enable_2, IC1.+V
  N2: Raspberry_Pi1.GND, IC1.0V
  N3: Raspberry_Pi1.GPIO_23, IC1.In_1
  N4: Raspberry_Pi1.GPIO_24, IC1.In_2
  N5: Raspberry_Pi1.GPIO_8, IC1.In_3
  N6: Raspberry_Pi1.GPIO_7, IC1.In_4
  N7: IC1.Out_1_(_Controlled_by_Enable_1_), M1.B
  N8: IC1.Out_2_(_Controlled_by_Enable_1_), M1.D
  N9: IC1.Out_3_(_Controlled_by_Enable_2_), M1.A
  N10: IC1.Out_4_(_Controlled_by_Enable_2_), M1.C
